# Fritzing sketch rylr (saved by Fritzing 0.9.3b)

parts:
  Mod1 = RYLR896 [package=THT]
  S1 = Square Pushbutton
  A1 = 2x18650 battery shield [package=THT]
  Part1 = Arduino Nano (Rev3.0) (ICSP)
  Mod2 = RYLR896 [package=THT]
  A2 = 2x18650 battery shield [package=THT]
  Part2 = Arduino Nano (Rev3.0) (ICSP)
  Mod3 = KY-016 RGB Full Color LED Module [package="Breakout board"]
  Mod6 = KY-016 RGB Full Color LED Module [package="Breakout board"]
  Part4 = Arduino Nano (Rev3.0) (ICSP)
  Part3 = Arduino Nano (Rev3.0) (ICSP)
  Mod5 = RYLR896 [package=THT]
  A4 = 2x18650 battery shield [package=THT]
  Mod4 = RYLR896 [package=THT]
  A3 = 2x18650 battery shield [package=THT]
  S2 = Square Pushbutton

nets:
  N1: Mod1.pin1, Part1.3V3
  N2: Mod1.pin3#2, Part1.A5
  N3: Mod1.pin3#3, Part1.A4
  N4: Mod1.pin5, S1.leg0, A1.pin_2, A1.pin_6, Part1.GND, Mod3.-
  N5: S1.leg1, Part1.D4
  N6: A1.pin_1, A1.pin_9, Part1.VIN
  N7: Part1.D6, Mod3.B
  N8: Part1.D7, Mod3.G
  N9: Part1.D8, Mod3.R
  N10: Mod2.pin1, Part2.3V3
  N11: Mod2.pin3#2, Part2.A5
  N12: Mod2.pin3#3, Part2.A4
  N13: Mod2.pin5, A2.pin_2, A2.pin_10, Part2.GND
  N14: A2.pin_1, A2.pin_9, Part2.VIN
  N15: Mod6.R, Part3.D8
  N16: Mod6.G, Part3.D7
  N17: Mod6.B, Part3.D6
  N18: Mod6.-, Part3.GND, A4.pin_2, A4.pin_6, Mod4.pin5, S2.leg0
  N19: Part4.VIN, A3.pin_1, A3.pin_9
  N20: Part4.GND, Mod5.pin5, A3.pin_2, A3.pin_10
  N21: Part4.A5, Mod5.pin3#2
  N22: Part4.A4, Mod5.pin3#3
  N23: Part4.3V3, Mod5.pin1
  N24: Part3.D4, S2.leg1
  N25: Part3.VIN, A4.pin_1, A4.pin_9
  N26: Part3.A5, Mod4.pin3#2
  N27: Part3.A4, Mod4.pin3#3
  N28: Part3.3V3, Mod4.pin1

custom parts:
  RYLR896: RYLR896 UART Interface 868/915mhz LORA Transceiver Module
  2x18650 battery shield: 2x18650 Lithium Battery Shield V9 CC CV Type-C Micro USB Mobile Power Bank DIY Module 5V 3A 3V 1A for iPhone Samsung Xiaomi.
  KY-016 RGB Full Color LED Module: KY-016 Arduino full color 5mm RGB LED, different colors can be obtained by mixing the three primary colors.
